// Logisim project Question2_simplified logic circuit.circ as structural Verilog: 1 circuit, main circuit main
module main (
  input  A,
  input  B,
  input  C,
  input  D,
  output F
);

  wire and_1_out, and_2_out, and_3_out, and_4_out, not_1_out, not_2_out, not_3_out, not_4_out, not_5_out;

  not not_1 (not_1_out, C);
  not not_2 (not_2_out, A);
  not not_3 (not_3_out, D);
  not not_4 (not_4_out, A);
  not not_5 (not_5_out, C);
  and and_1 (and_1_out, D, C, A);
  and and_2 (and_2_out, D, not_5_out, B);
  and and_3 (and_3_out, not_3_out, not_4_out);
  and and_4 (and_4_out, not_1_out, not_2_out);
  or or_1 (F, and_1_out, and_2_out, and_3_out, and_4_out);

  // Notes on the sheet:
  //   SIMPLIFIED VERSION OF F = A'B'C'D + BC'D + D'A' + CDA
  //   F = A'C' + A'D' + BC'D + ACD
  //   ACD
  //   BC'D
  //   A'D'
  //   A'C'
endmodule
