// Logisim project Question3_6 bit Asynchronous counter.circ as structural Verilog: 1 circuit, main circuit main
module main (
  input  in_1,
  input  SET,
  input  ENABLE,
  input  RESET,
  output out_5,
  output out_6,
  output out_7,
  output out_8,
  output out_9,
  output out_10
);

  wire clock_1_out, j_k_ff_1_q, j_k_ff_2_q, j_k_ff_3_q, j_k_ff_4_q, j_k_ff_5_q;

  Clock clock_1 (.out(clock_1_out));
  J_K_Flip_Flop j_k_ff_1 (
    .J(in_1), .clk(clock_1_out), .K(in_1), .Q(j_k_ff_1_q), .Qn(out_10), .preset(SET), .en(ENABLE),
    .reset(RESET));
  J_K_Flip_Flop j_k_ff_2 (
    .J(in_1), .clk(j_k_ff_1_q), .K(in_1), .Q(j_k_ff_2_q), .Qn(out_9), .preset(SET), .en(ENABLE), .reset(RESET));
  J_K_Flip_Flop j_k_ff_3 (
    .J(in_1), .clk(j_k_ff_2_q), .K(in_1), .Q(j_k_ff_3_q), .Qn(out_8), .preset(SET), .en(ENABLE), .reset(RESET));
  J_K_Flip_Flop j_k_ff_4 (
    .J(in_1), .clk(j_k_ff_3_q), .K(in_1), .Q(j_k_ff_4_q), .Qn(out_7), .preset(SET), .en(ENABLE), .reset(RESET));
  J_K_Flip_Flop j_k_ff_5 (
    .J(in_1), .clk(j_k_ff_4_q), .K(in_1), .Q(j_k_ff_5_q), .Qn(out_6), .preset(SET), .en(ENABLE), .reset(RESET));
  J_K_Flip_Flop j_k_ff_6 (
    .J(in_1), .clk(j_k_ff_5_q), .K(in_1), .Qn(out_5), .preset(SET), .en(ENABLE), .reset(RESET));  // open: Q

  // Notes on the sheet:
  //   CLK
  //   A
  //   B
  //   6-bit Asynchronous Up Counter using JK flip-flops
  //   C
  //   D
  //   E
  //   F
  //   MSB
  //   LSB
endmodule
