// Logisim project 5-bit_Register_Set_with_4_Registers_Library.circ as structural Verilog: 4 circuits, main circuit 1-bit Register
module _1_bit_Register (
  input  Din,
  input  Sel,
  input  Clock,
  output Dout
);

  wire multiplexer_1_out;

  Multiplexer #(.enable("false")) multiplexer_1 (.in0(Dout), .in1(Din), .out(multiplexer_1_out), .sel(Sel));
  D_Flip_Flop d_ff_1 (.clk(Clock), .D(multiplexer_1_out), .Q(Dout));  // open: Qn, preset, en, reset

  // Notes on the sheet:
  //   1-bit Register
endmodule

module _5_bit_Register (
  input  [4:0] Din_4_0,
  input  Sel,
  input  Clock,
  output [4:0] Dout_6_0
);

  _1_bit_Register u_1_bit_register_1 (.Din(Din_4_0[0]), .Sel(Sel), .Clock(Clock), .Dout(Dout_6_0[0]));
  _1_bit_Register u_1_bit_register_2 (.Din(Din_4_0[1]), .Sel(Sel), .Clock(Clock), .Dout(Dout_6_0[1]));
  _1_bit_Register u_1_bit_register_3 (.Din(Din_4_0[2]), .Sel(Sel), .Clock(Clock), .Dout(Dout_6_0[2]));
  _1_bit_Register u_1_bit_register_4 (.Din(Din_4_0[3]), .Sel(Sel), .Clock(Clock), .Dout(Dout_6_0[3]));
  _1_bit_Register u_1_bit_register_5 (.Din(Din_4_0[4]), .Sel(Sel), .Clock(Clock), .Dout(Dout_6_0[4]));

  // Notes on the sheet:
  //   5-bit Register
endmodule

module _5_bit_Register_Set_with_4_Registers (
  input  [1:0] Ra,
  input  REG_EN,
  input  [1:0] Wr,
  input  [4:0] Wrd,
  input  Clock,
  input  [1:0] Rb,
  output [4:0] A,
  output [4:0] B
);

  wire Reg0, Reg1, Reg2, Reg3;
  wire [4:0] R0, R1, R2, R3;

  Decoder #(.select(2)) decoder_1 (.out0(Reg0), .out1(Reg1), .out2(Reg2), .out3(Reg3), .sel(Wr), .en(REG_EN));
  _5_bit_Register u_5_bit_register_1 (.Din_4_0(Wrd), .Sel(Reg0), .Clock(Clock), .Dout_6_0(R0));
  _5_bit_Register u_5_bit_register_2 (.Din_4_0(Wrd), .Sel(Reg1), .Clock(Clock), .Dout_6_0(R1));
  _5_bit_Register u_5_bit_register_3 (.Din_4_0(Wrd), .Sel(Reg2), .Clock(Clock), .Dout_6_0(R2));
  _5_bit_Register u_5_bit_register_4 (.Din_4_0(Wrd), .Sel(Reg3), .Clock(Clock), .Dout_6_0(R3));
  Multiplexer #(.select(2), .width(5), .enable("false")) multiplexer_1 (
    .in0(R0), .in1(R1), .in2(R2), .in3(R3), .out(A), .sel(Ra));
  Multiplexer #(.select(2), .width(5), .enable("false")) multiplexer_2 (
    .in0(R0), .in1(R1), .in2(R2), .in3(R3), .out(B), .sel(Rb));

  // Notes on the sheet:
  //   5-bit 2 to 4 Decoder
  //   Register0
  //   Register0
  //   Register1
  //   Register2
  //   Register3
  //   5-bit Register Set with 4 Registers
  //   5-bit 4 to 1 MUX
  //   5-bit 4 to 1 MUX
endmodule

module Register_Set_Test (
  input  [1:0] Ra,
  input  [1:0] Rb,
  input  REG_EN,
  input  [1:0] Wr,
  input  [4:0] Wrd,
  input  Clock,
  output [4:0] A,
  output [4:0] B
);

  _5_bit_Register_Set_with_4_Registers u_5_bit_register_set_with_4_registers_1 (
    .REG_EN(REG_EN), .Wr(Wr), .Wrd(Wrd), .Clock(Clock), .Ra(Ra), .Rb(Rb), .A(A), .B(B));
endmodule
