// Logisim project 1-bit Register.circ as structural Verilog: 1 circuit, main circuit main
module main (
  input  Din,
  input  Sel,
  input  Clock,
  output Dout
);

  wire multiplexer_1_out;

  Multiplexer #(.enable("false")) multiplexer_1 (.in0(Dout), .in1(Din), .out(multiplexer_1_out), .sel(Sel));
  D_Flip_Flop d_ff_1 (.clk(Clock), .D(multiplexer_1_out), .Q(Dout));  // open: Qn, preset, en, reset

  // Notes on the sheet:
  //   1-bit Register
endmodule
