// Logisim project 5-bit 2 to 1 MUX.circ as structural Verilog: 1 circuit, main circuit main
module main (
  input  [4:0] A,
  input  [4:0] B,
  input  S,
  output [4:0] O
);

  Multiplexer #(.enable("false")) multiplexer_1 (.in0(A[4]), .in1(B[4]), .out(O[4]), .sel(S));
  Multiplexer #(.enable("false")) multiplexer_2 (.in0(A[3]), .in1(B[3]), .out(O[3]), .sel(S));
  Multiplexer #(.enable("false")) multiplexer_3 (.in0(A[2]), .in1(B[2]), .out(O[2]), .sel(S));
  Multiplexer #(.enable("false")) multiplexer_4 (.in0(A[1]), .in1(B[1]), .out(O[1]), .sel(S));
  Multiplexer #(.enable("false")) multiplexer_5 (.in0(A[0]), .in1(B[0]), .out(O[0]), .sel(S));

  // Notes on the sheet:
  //   5-bit 2 to 1 MUX
endmodule
