// Logisim project 5-bit ALU.circ as structural Verilog: 1 circuit, main circuit main
module main (
  input  Op,
  input  [4:0] A_4_0,
  input  [4:0] B_4_0,
  output [4:0] R_4_0,
  output Sign_Flag,
  output Zero_Flag
);

  wire or_1_out;
  wire [4:0] ROL, SHL;

  _5_bit_Left_Shift_main main_1 (.A(A_4_0), .O(SHL), .Shift(B_4_0[2:0]));
  _5_bit_Left_Rotate_main main_2 (.A(A_4_0), .O(ROL), .Shift(B_4_0[2:0]));
  _5_bit_2_to_1_MUX_main main_3 (.A(SHL), .B(ROL), .S(Op), .O(R_4_0));
  not not_1 (Zero_Flag, or_1_out);
  or or_1 (or_1_out, R_4_0[0], R_4_0[1], R_4_0[2], R_4_0[3], R_4_0[4]);

  assign Sign_Flag = R_4_0[4];

  // Other names for the same wires on the sheet: A[4:0] = A_4_0; B[4:0] = B_4_0; Shift[2:0] = B_4_0[2:0]

  // Notes on the sheet:
  //   5-bit ALU with 2 Operations
endmodule
