// Logisim project 5-bit Flag Registers.circ as structural Verilog: 1 circuit, main circuit main
module main (
  input  SF,
  input  ZF,
  input  Clock,
  output SF_2,
  output ZF_2
);

  _1_bit_Register_main main_1 (.Din(SF), .Sel(1'b1), .Clock(Clock), .Dout(SF_2));
  _1_bit_Register_main main_2 (.Din(ZF), .Sel(1'b1), .Clock(Clock), .Dout(ZF_2));

  // Notes on the sheet:
  //   FLAG Register
endmodule
