// Logisim project 5-bit Left Rotate.circ as structural Verilog: 1 circuit, main circuit main
module main (
  input  [4:0] A,
  input  [2:0] Shift,
  output [4:0] O
);

  Multiplexer #(.select(3), .enable("false")) multiplexer_1 (
    .in0(A[4]), .in1(A[3]), .in2(A[2]), .in3(A[1]), .in4(A[0]), .in5(A[4]), .in6(A[3]), .in7(A[2]),
    .out(O[4]), .sel(Shift));
  Multiplexer #(.select(3), .enable("false")) multiplexer_2 (
    .in0(A[3]), .in1(A[2]), .in2(A[1]), .in3(A[0]), .in4(A[4]), .in5(A[3]), .in6(A[2]), .in7(A[1]),
    .out(O[3]), .sel(Shift));
  Multiplexer #(.select(3), .enable("false")) multiplexer_3 (
    .in0(A[2]), .in1(A[1]), .in2(A[0]), .in3(A[4]), .in4(A[3]), .in5(A[2]), .in6(A[1]), .in7(A[0]),
    .out(O[2]), .sel(Shift));
  Multiplexer #(.select(3), .enable("false")) multiplexer_4 (
    .in0(A[1]), .in1(A[0]), .in2(A[4]), .in3(A[3]), .in4(A[2]), .in5(A[1]), .in6(A[0]), .in7(A[4]),
    .out(O[1]), .sel(Shift));
  Multiplexer #(.select(3), .enable("false")) multiplexer_5 (
    .in0(A[0]), .in1(A[4]), .in2(A[3]), .in3(A[2]), .in4(A[1]), .in5(A[0]), .in6(A[4]), .in7(A[3]),
    .out(O[0]), .sel(Shift));

  // Notes on the sheet:
  //   5-bit Left Rotate
endmodule
