// Logisim project 5-bit Register Set with 4 Registers.circ as structural Verilog: 1 circuit, main circuit main
module main (
  input  REG_EN,
  input  [1:0] Wr,
  input  [4:0] Wrd,
  input  [4:0] Input_Data,
  input  Input_EN,
  input  Clock,
  input  [1:0] Ra,
  input  [1:0] Rb,
  output [4:0] A,
  output [4:0] B,
  output [4:0] Output_Data
);

  wire Reg0, Reg1, Reg2, Reg3;
  wire [4:0] R0, R1, R3;

  Decoder #(.select(2)) decoder_1 (.out0(Reg0), .out1(Reg1), .out2(Reg2), .out3(Reg3), .sel(Wr), .en(REG_EN));
  _5_bit_Register_main main_1 (.Din_4_0(Wrd), .Sel(Reg0), .Clock(Clock), .Dout_6_0(R0));
  _5_bit_Register_main main_2 (.Din_4_0(Wrd), .Sel(Reg1), .Clock(Clock), .Dout_6_0(R1));
  _5_bit_Register_main main_3 (.Din_4_0(Wrd), .Sel(Reg2), .Clock(Clock), .Dout_6_0(Output_Data));
  _5_bit_Register_main main_4 (.Din_4_0(Input_Data), .Sel(Input_EN), .Clock(Clock), .Dout_6_0(R3));
  Multiplexer #(.select(2), .width(5), .enable("false")) multiplexer_1 (
    .in0(R0), .in1(R1), .in2(Output_Data), .in3(R3), .out(A), .sel(Ra));
  Multiplexer #(.select(2), .width(5), .enable("false")) multiplexer_2 (
    .in0(R0), .in1(R1), .in2(Output_Data), .in3(R3), .out(B), .sel(Rb));

  // Other names for the same wires on the sheet: R2[4:0] = Output_Data

  // Notes on the sheet:
  //   5-bit 2 to 4 Decoder
  //   5-bit Register Set with 4 Registers
  //   Register0
  //   Register0
  //   STACK REGISTER
  //   OUTPUT REGISTER
  //   INPUT REGISTER
  //   5-bit 4 to 1 MUX
  //   5-bit 4 to 1 MUX
endmodule
