// Logisim project 5-bit Register.circ as structural Verilog: 1 circuit, main circuit main
module main (
  input  [4:0] Din_4_0,
  input  Sel,
  input  Clock,
  output [4:0] Dout_6_0
);

  _1_bit_Register_main main_1 (.Din(Din_4_0[0]), .Sel(Sel), .Clock(Clock), .Dout(Dout_6_0[0]));
  _1_bit_Register_main main_2 (.Din(Din_4_0[1]), .Sel(Sel), .Clock(Clock), .Dout(Dout_6_0[1]));
  _1_bit_Register_main main_3 (.Din(Din_4_0[2]), .Sel(Sel), .Clock(Clock), .Dout(Dout_6_0[2]));
  _1_bit_Register_main main_4 (.Din(Din_4_0[3]), .Sel(Sel), .Clock(Clock), .Dout(Dout_6_0[3]));
  _1_bit_Register_main main_5 (.Din(Din_4_0[4]), .Sel(Sel), .Clock(Clock), .Dout(Dout_6_0[4]));

  // Notes on the sheet:
  //   5-bit Register
endmodule
