// Logisim project 5-bit_ALU_with_2_Operations_Library.circ as structural Verilog: 4 circuits, main circuit ALU
module SHL (
  input  [4:0] A_4_0,
  input  [2:0] Shift,
  output [4:0] O_4_0
);

  Multiplexer #(.select(3), .enable("false")) multiplexer_1 (
    .in0(A_4_0[4]), .in1(A_4_0[3]), .in2(A_4_0[2]), .in3(A_4_0[1]), .in4(A_4_0[0]), .in5(1'b0), .in6(1'b0),
    .in7(1'b0), .out(O_4_0[4]), .sel(Shift));
  Multiplexer #(.select(3), .enable("false")) multiplexer_2 (
    .in0(A_4_0[3]), .in1(A_4_0[2]), .in2(A_4_0[1]), .in3(A_4_0[0]), .in4(1'b0), .in5(1'b0), .in6(1'b0),
    .in7(1'b0), .out(O_4_0[3]), .sel(Shift));
  Multiplexer #(.select(3), .enable("false")) multiplexer_3 (
    .in0(A_4_0[2]), .in1(A_4_0[1]), .in2(A_4_0[0]), .in3(1'b0), .in4(1'b0), .in5(1'b0), .in6(1'b0),
    .in7(1'b0), .out(O_4_0[2]), .sel(Shift));
  Multiplexer #(.select(3), .enable("false")) multiplexer_4 (
    .in0(A_4_0[1]), .in1(A_4_0[0]), .in2(1'b0), .in3(1'b0), .in4(1'b0), .in5(1'b0), .in6(1'b0), .in7(1'b0),
    .out(O_4_0[1]), .sel(Shift));
  Multiplexer #(.select(3), .enable("false")) multiplexer_5 (
    .in0(A_4_0[0]), .in1(1'b0), .in2(1'b0), .in3(1'b0), .in4(1'b0), .in5(1'b0), .in6(1'b0), .in7(1'b0),
    .out(O_4_0[0]), .sel(Shift));

  // Other names for the same wires on the sheet: A0 = A_4_0[0]; A1 = A_4_0[1]; A2 = A_4_0[2]; A3 = A_4_0[3];
  //   A4 = A_4_0[4]; O0 = O_4_0[0]; O1 = O_4_0[1]; O2 = O_4_0[2]; O3 = O_4_0[3]; O4 = O_4_0[4]

  // Notes on the sheet:
  //   5-bit Left Shift
endmodule

module ROL (
  input  [4:0] A_4_0,
  input  [2:0] Shift,
  output [4:0] O_4_0
);

  Multiplexer #(.select(3), .enable("false")) multiplexer_1 (
    .in0(A_4_0[4]), .in1(A_4_0[3]), .in2(A_4_0[2]), .in3(A_4_0[1]), .in4(A_4_0[0]), .in5(A_4_0[4]),
    .in6(A_4_0[3]), .in7(A_4_0[2]), .out(O_4_0[4]), .sel(Shift));
  Multiplexer #(.select(3), .enable("false")) multiplexer_2 (
    .in0(A_4_0[3]), .in1(A_4_0[2]), .in2(A_4_0[1]), .in3(A_4_0[0]), .in4(A_4_0[4]), .in5(A_4_0[3]),
    .in6(A_4_0[2]), .in7(A_4_0[1]), .out(O_4_0[3]), .sel(Shift));
  Multiplexer #(.select(3), .enable("false")) multiplexer_3 (
    .in0(A_4_0[2]), .in1(A_4_0[1]), .in2(A_4_0[0]), .in3(A_4_0[4]), .in4(A_4_0[3]), .in5(A_4_0[2]),
    .in6(A_4_0[1]), .in7(A_4_0[0]), .out(O_4_0[2]), .sel(Shift));
  Multiplexer #(.select(3), .enable("false")) multiplexer_4 (
    .in0(A_4_0[1]), .in1(A_4_0[0]), .in2(A_4_0[4]), .in3(A_4_0[3]), .in4(A_4_0[2]), .in5(A_4_0[1]),
    .in6(A_4_0[0]), .in7(A_4_0[4]), .out(O_4_0[1]), .sel(Shift));
  Multiplexer #(.select(3), .enable("false")) multiplexer_5 (
    .in0(A_4_0[0]), .in1(A_4_0[4]), .in2(A_4_0[3]), .in3(A_4_0[2]), .in4(A_4_0[1]), .in5(A_4_0[0]),
    .in6(A_4_0[4]), .in7(A_4_0[3]), .out(O_4_0[0]), .sel(Shift));

  // Other names for the same wires on the sheet: A0 = A_4_0[0]; A1 = A_4_0[1]; A2 = A_4_0[2]; A3 = A_4_0[3];
  //   A4 = A_4_0[4]; O0 = O_4_0[0]; O1 = O_4_0[1]; O2 = O_4_0[2]; O3 = O_4_0[3]; O4 = O_4_0[4]

  // Notes on the sheet:
  //   5-bit Left Rotate
endmodule

module ALU (
  input  Op,
  input  [4:0] A_4_0,
  input  [4:0] B_4_0,
  output [4:0] R_4_0,
  output Sign_FLAG,
  output Zero_FLAG
);

  wire or_1_out;
  wire [4:0] ROL, SHL;

  SHL shl_1 (.A_4_0(A_4_0), .O_4_0(SHL), .Shift(B_4_0[2:0]));
  ROL rol_1 (.A_4_0(A_4_0), .O_4_0(ROL), .Shift(B_4_0[2:0]));
  Multiplexer #(.width(5), .enable("false")) multiplexer_1 (.in0(SHL), .in1(ROL), .out(R_4_0), .sel(Op));
  or or_1 (or_1_out, R_4_0[0], R_4_0[1], R_4_0[2], R_4_0[3], R_4_0[4]);
  not not_1 (Zero_FLAG, or_1_out);

  assign Sign_FLAG = R_4_0[4];

  // Other names for the same wires on the sheet: A[4:0] = A_4_0; B[4:0] = B_4_0; Shift[2:0] = B_4_0[2:0]

  // Notes on the sheet:
  //   5-bit ALU with 2 Operations
  //   5-bit 2 to 1 MUX
endmodule

module ALU_Test (
  input  [4:0] A_4_0,
  input  [4:0] B_4_0,
  input  Op,
  output [4:0] R_4_0,
  output Sign_FLAG,
  output Zero_FLAG
);

  ALU alu_1 (.A_4_0(A_4_0), .B_4_0(B_4_0), .R_4_0(R_4_0), .Sign_FLAG(Sign_FLAG), .Zero_FLAG(Zero_FLAG), .Op(Op));
endmodule
