// Logisim project 5-bit_CPU_Library.circ as structural Verilog: 4 circuits, main circuit 3-bit Counter Register
module _3_bit_Counter_Register (
  input  [2:0] I__2_0,
  input  Clock,
  output [2:0] O__2_0
);

  D_Flip_Flop d_ff_1 (.clk(Clock), .D(I__2_0[0]), .Q(O__2_0[0]));  // open: Qn, preset, en, reset
  D_Flip_Flop d_ff_2 (.clk(Clock), .D(I__2_0[1]), .Q(O__2_0[1]));  // open: Qn, preset, en, reset
  D_Flip_Flop d_ff_3 (.clk(Clock), .D(I__2_0[2]), .Q(O__2_0[2]));  // open: Qn, preset, en, reset

  // Notes on the sheet:
  //   3-bit Counter Register
endmodule

module PC_Adder (
  input  [2:0] Input_Address_2_0,
  output [2:0] Output_Address__2_0
);

  wire [2:0] bit_extender_1_out;

  assign bit_extender_1_out = {{2{1'b0}}, 1'b1};  // Bit_Extender bit_extender_1
  Adder #(.width(3)) adder_1 (
    .a(Input_Address_2_0), .b(bit_extender_1_out), .out(Output_Address__2_0), .cin(1'b0));  // open: cout
endmodule

module Control_Unit (
  input  [2:0] Opcode__2_0,
  output Op,
  output Imm_Sel,
  output WE,
  output Jmp_Sel
);

  wire and_2_out, and_3_out, not_1_out, not_2_out, not_3_out, not_4_out, not_5_out;

  not not_1 (not_1_out, Opcode__2_0[2]);
  not not_2 (not_2_out, Opcode__2_0[2]);
  not not_3 (not_3_out, Opcode__2_0[1]);
  not not_4 (not_4_out, Opcode__2_0[1]);
  not not_5 (not_5_out, Opcode__2_0[0]);
  and and_1 (Imm_Sel, not_1_out, Opcode__2_0[1]);
  and and_2 (and_2_out, not_2_out, not_3_out);
  and and_3 (and_3_out, Opcode__2_0[2], not_4_out);
  or or_1 (WE, Imm_Sel, and_2_out);
  and and_4 (Jmp_Sel, and_3_out, not_5_out);

  assign Op = Opcode__2_0[0];
endmodule

module CPU__Upto_Branching (
  input  [2:0] Write_Address__2_0,
  input  [14:0] Write_Data__14_0,
  input  Write_Enable,
  input  Clock,
  input  CPU_Enable
);

  wire CPU_CLK, Imm_Sel, Jmp_Sel, Op, WE;
  wire [2:0] JMP_Addr, multiplexer_1_out, n3_bit_counter_register_1_o__2_0, pc_adder_1_output_address__2_0;
  wire [4:0] alu_1_r_4_0, multiplexer_2_out, n5_bit_register_set_with_4_registers_1_a,
       n5_bit_register_set_with_4_registers_1_b;
  wire [14:0] n7x15_sram_1_read_data_1__14_0;

  PC_Adder pc_adder_1 (
    .Input_Address_2_0(n3_bit_counter_register_1_o__2_0), .Output_Address__2_0(pc_adder_1_output_address__2_0));
  Multiplexer #(.width(3), .enable("false")) multiplexer_1 (
    .in0(pc_adder_1_output_address__2_0), .in1(JMP_Addr), .out(multiplexer_1_out), .sel(Jmp_Sel));
  _3_bit_Counter_Register u_3_bit_counter_register_1 (
    .I__2_0(multiplexer_1_out), .Clock(CPU_CLK), .O__2_0(n3_bit_counter_register_1_o__2_0));
  _7x15_SRAM u_7x15_sram_1 (
    .Write_Data__14_0(Write_Data__14_0), .Write_Enable(Write_Enable),
    .Write_Address__2_0(Write_Address__2_0), .Read_Address_1__2_0(n3_bit_counter_register_1_o__2_0),
    .Clock(Clock),
    .Read_Data_1__14_0({n7x15_sram_1_read_data_1__14_0[14:12], JMP_Addr, n7x15_sram_1_read_data_1__14_0[8:0]}));  // open: Read_Address_2__2_0, Read_Data_2__14_0
  and and_1 (CPU_CLK, Clock, CPU_Enable);
  _5_bit_Register_Set_with_4_Registers u_5_bit_register_set_with_4_registers_1 (
    .REG_EN(WE), .Wr(JMP_Addr[2:1]), .Wrd(alu_1_r_4_0), .Clock(CPU_CLK), .Ra(JMP_Addr[2:1]),
    .Rb({JMP_Addr[0], n7x15_sram_1_read_data_1__14_0[8]}), .A(n5_bit_register_set_with_4_registers_1_a),
    .B(n5_bit_register_set_with_4_registers_1_b));
  Multiplexer #(.width(5), .enable("false")) multiplexer_2 (
    .in0(n5_bit_register_set_with_4_registers_1_b), .in1({JMP_Addr[0], n7x15_sram_1_read_data_1__14_0[8:5]}),
    .out(multiplexer_2_out), .sel(Imm_Sel));
  ALU alu_1 (.A_4_0(n5_bit_register_set_with_4_registers_1_a), .B_4_0(multiplexer_2_out), .R_4_0(alu_1_r_4_0), .Op(Op));
  Control_Unit control_unit_1 (
    .Opcode__2_0(n7x15_sram_1_read_data_1__14_0[14:12]), .Op(Op), .Imm_Sel(Imm_Sel), .WE(WE),
    .Jmp_Sel(Jmp_Sel));

  // Other names for the same wires on the sheet: CLK = Clock

  // Notes on the sheet:
  //   Register Mode SHL 000101100000000
  //   Immediate Mode SHL 010100000100000
  //   Branching Mode JMP 100011000000000
  //   Branching Mode: Opcode (2 bits + 1 bit) + Address (3 bits) + Unused (9 bits) ---> Opcode 1st 2 bits = 10 + Opcode last 1 bit = JMP (0)  
  //   5-bit CPU
  //   Register Mode: Opcode (2 bits + 1 bit) + Register RA (2 bits) + Register RB (2 bits) + Unused (8 bits) ---> Opcode 1st 2 bits = 00 + Opcode last 1 bit = SHL (0), ROL(1)  
  //   Register Mode ROL 001100100000000
  //   Immediate Mode: Opcode (2 bits + 1 bit) + Register RA (2 bits) + Immediate Value (5 bits) + Unused (5 bits) ---> Opcode 1st 2 bits = 01 + Opcode last 1 bit = SHL (0), ROL(1)  
  //   Immediate Mode ROL 011110000100000
endmodule
