// Logisim project 7x15_RAM_Library.circ as structural Verilog: 5 circuits, main circuit 1x1 Static RAM cell
module _1x1_Static_RAM_cell (
  input  Read_Select_1,
  input  Read_Select_2,
  input  Write_Data,
  input  Write_Select,
  input  Clock,
  output Read_Data_1,
  output Read_Data_2
);

  wire d_ff_1_q, multiplexer_1_out;

  Multiplexer #(.enable("false")) multiplexer_1 (
    .in0(d_ff_1_q), .in1(Write_Data), .out(multiplexer_1_out), .sel(Write_Select));
  D_Flip_Flop d_ff_1 (.clk(Clock), .D(multiplexer_1_out), .Q(d_ff_1_q));  // open: Qn, preset, en, reset
  and and_1 (Read_Data_1, Read_Select_1, d_ff_1_q);
  and and_2 (Read_Data_2, Read_Select_2, d_ff_1_q);

  // Notes on the sheet:
  //   1x1 Static RAM Cell
endmodule

module _1x3_SRAM (
  input  Read_Select_1,
  input  Read_Select_2,
  input  Write_Select,
  input  [2:0] Write_Data,
  input  Clock,
  output [2:0] Read_Data_1,
  output [2:0] Read_Data_2
);

  _1x1_Static_RAM_cell u_1x1_static_ram_cell_1 (
    .Write_Data(Write_Data[0]), .Write_Select(Write_Select), .Clock(Clock), .Read_Data_1(Read_Data_1[0]),
    .Read_Data_2(Read_Data_2[0]), .Read_Select_1(Read_Select_1), .Read_Select_2(Read_Select_2));
  _1x1_Static_RAM_cell u_1x1_static_ram_cell_2 (
    .Write_Data(Write_Data[1]), .Write_Select(Write_Select), .Clock(Clock), .Read_Data_1(Read_Data_1[1]),
    .Read_Data_2(Read_Data_2[1]), .Read_Select_1(Read_Select_1), .Read_Select_2(Read_Select_2));
  _1x1_Static_RAM_cell u_1x1_static_ram_cell_3 (
    .Write_Data(Write_Data[2]), .Write_Select(Write_Select), .Clock(Clock), .Read_Data_1(Read_Data_1[2]),
    .Read_Data_2(Read_Data_2[2]), .Read_Select_1(Read_Select_1), .Read_Select_2(Read_Select_2));

  // Notes on the sheet:
  //   1x3 Static RAM Cell
endmodule

module _1x15_SRAM (
  input  Read_Select_1,
  input  Read_Select_2,
  input  Write_Select,
  input  Clock,
  input  [14:0] Write_Data,
  output [14:0] Read_Data_1__14_0,
  output [14:0] Read_Data_2__14_0
);

  _1x3_SRAM u_1x3_sram_1 (
    .Read_Select_1(Read_Select_1), .Read_Select_2(Read_Select_2), .Write_Select(Write_Select),
    .Write_Data(Write_Data[2:0]), .Clock(Clock), .Read_Data_1(Read_Data_1__14_0[2:0]),
    .Read_Data_2(Read_Data_2__14_0[2:0]));
  _1x3_SRAM u_1x3_sram_2 (
    .Read_Select_1(Read_Select_1), .Read_Select_2(Read_Select_2), .Write_Select(Write_Select),
    .Write_Data(Write_Data[5:3]), .Clock(Clock), .Read_Data_1(Read_Data_1__14_0[5:3]),
    .Read_Data_2(Read_Data_2__14_0[5:3]));
  _1x3_SRAM u_1x3_sram_3 (
    .Read_Select_1(Read_Select_1), .Read_Select_2(Read_Select_2), .Write_Select(Write_Select),
    .Write_Data(Write_Data[8:6]), .Clock(Clock), .Read_Data_1(Read_Data_1__14_0[8:6]),
    .Read_Data_2(Read_Data_2__14_0[8:6]));
  _1x3_SRAM u_1x3_sram_4 (
    .Read_Select_1(Read_Select_1), .Read_Select_2(Read_Select_2), .Write_Select(Write_Select),
    .Write_Data(Write_Data[11:9]), .Clock(Clock), .Read_Data_1(Read_Data_1__14_0[11:9]),
    .Read_Data_2(Read_Data_2__14_0[11:9]));
  _1x3_SRAM u_1x3_sram_5 (
    .Read_Select_1(Read_Select_1), .Read_Select_2(Read_Select_2), .Write_Select(Write_Select),
    .Write_Data(Write_Data[14:12]), .Clock(Clock), .Read_Data_1(Read_Data_1__14_0[14:12]),
    .Read_Data_2(Read_Data_2__14_0[14:12]));

  // Notes on the sheet:
  //   1x15 Static RAM Cell
endmodule

module _7x15_SRAM (
  input  [2:0] Read_Address_1__2_0,
  input  [2:0] Read_Address_2__2_0,
  input  Write_Enable,
  input  [2:0] Write_Address__2_0,
  input  [14:0] Write_Data__14_0,
  input  Clock,
  output [14:0] Read_Data_1__14_0,
  output [14:0] Read_Data_2__14_0
);

  wire R1_0, R1_1, R1_2, R1_3, R1_4, R1_5, R1_6, R2_0, R2_0_t, R2_1, R2_1_t, R2_2, R2_3, R2_4, R2_4_t, R2_5,
       R2_5_t, R2_6, W0, W1, W2, W3, W4, W5, W6;
  wire [14:0] RD1_0, RD1_1, RD1_2, RD1_3, RD1_4, RD1_5, RD1_6, RD2_0, RD2_1, RD2_2, RD2_3, RD2_4, RD2_5,
       RD2_6;

  Decoder #(.select(3), .disabled(0), .enable("false")) decoder_1 (
    .out0(R1_0), .out1(R1_1), .out2(R1_2), .out3(R1_3), .out4(R1_4), .out5(R1_5), .out6(R1_6),
    .sel(Read_Address_1__2_0));  // open: out7
  Decoder #(.select(3), .disabled(0), .enable("false")) decoder_2 (
    .out0(R2_0_t), .out1(R2_1_t), .out2(R2_2), .out3(R2_3), .out4(R2_4_t), .out5(R2_5_t), .out6(R2_6),
    .sel(Read_Address_2__2_0));  // open: out7
  Decoder #(.select(3), .disabled(0)) decoder_3 (
    .out0(W0), .out1(W1), .out2(W2), .out3(W3), .out4(W4), .out5(W5), .out6(W6), .sel(Write_Address__2_0),
    .en(Write_Enable));  // open: out7
  _1x15_SRAM u_1x15_sram_1 (
    .Read_Select_1(R1_0), .Read_Select_2(R2_0), .Write_Select(W0), .Clock(Clock),
    .Write_Data(Write_Data__14_0), .Read_Data_1__14_0(RD1_0), .Read_Data_2__14_0(RD2_0));
  _1x15_SRAM u_1x15_sram_2 (
    .Read_Select_1(R1_1), .Read_Select_2(R2_1), .Write_Select(W1), .Clock(Clock),
    .Write_Data(Write_Data__14_0), .Read_Data_1__14_0(RD1_1), .Read_Data_2__14_0(RD2_1));
  _1x15_SRAM u_1x15_sram_3 (
    .Read_Select_1(R1_2), .Read_Select_2(R2_2), .Write_Select(W2), .Clock(Clock),
    .Write_Data(Write_Data__14_0), .Read_Data_1__14_0(RD1_2), .Read_Data_2__14_0(RD2_2));
  _1x15_SRAM u_1x15_sram_4 (
    .Read_Select_1(R1_3), .Read_Select_2(R2_3), .Write_Select(W3), .Clock(Clock),
    .Write_Data(Write_Data__14_0), .Read_Data_1__14_0(RD1_3), .Read_Data_2__14_0(RD2_3));
  _1x15_SRAM u_1x15_sram_5 (
    .Read_Select_1(R1_4), .Read_Select_2(R2_4), .Write_Select(W4), .Clock(Clock),
    .Write_Data(Write_Data__14_0), .Read_Data_1__14_0(RD1_4), .Read_Data_2__14_0(RD2_4));
  _1x15_SRAM u_1x15_sram_6 (
    .Read_Select_1(R1_5), .Read_Select_2(R2_5), .Write_Select(W5), .Clock(Clock),
    .Write_Data(Write_Data__14_0), .Read_Data_1__14_0(RD1_5), .Read_Data_2__14_0(RD2_5));
  _1x15_SRAM u_1x15_sram_7 (
    .Read_Select_1(R1_6), .Read_Select_2(R2_6), .Write_Select(W6), .Clock(Clock),
    .Write_Data(Write_Data__14_0), .Read_Data_1__14_0(RD1_6), .Read_Data_2__14_0(RD2_6));
  assign Read_Data_1__14_0 = RD1_0 | RD1_1 | RD1_2 | RD1_3 | RD1_4 | RD1_5 | RD1_6;  // OR_Gate or_1, 15 bits wide
  assign Read_Data_2__14_0 = RD2_0 | RD2_1 | RD2_2 | RD2_3 | RD2_4 | RD2_5 | RD2_6;  // OR_Gate or_2, 15 bits wide

  // Notes on the sheet:
  //   7x15 Static RAM Cell
endmodule

module RAM_Test (
  input  [2:0] Read_Address_1__2_0,
  input  [2:0] Read_Address_2__2_0,
  input  [2:0] Write_Address__6_0,
  input  [14:0] Write_Data__14_0,
  input  Write_Enable,
  input  Clock,
  output [14:0] Read_Data_1__14_0,
  output [14:0] Read_Data_2__14_0
);

  _7x15_SRAM u_7x15_sram_1 (
    .Write_Data__14_0(Write_Data__14_0), .Write_Enable(Write_Enable),
    .Write_Address__2_0(Write_Address__6_0), .Read_Address_1__2_0(Read_Address_1__2_0),
    .Read_Address_2__2_0(Read_Address_2__2_0), .Clock(Clock), .Read_Data_1__14_0(Read_Data_1__14_0),
    .Read_Data_2__14_0(Read_Data_2__14_0));
endmodule
