// Logisim project 5-bit Left Shift.circ as structural Verilog: 1 circuit, main circuit main
module main (
  input  [4:0] A,
  input  [2:0] Shift,
  output [4:0] O
);

  Multiplexer #(.select(3), .enable("false")) multiplexer_1 (
    .in0(A[4]), .in1(A[3]), .in2(A[2]), .in3(A[1]), .in4(A[0]), .in5(1'b0), .in6(1'b0), .in7(1'b0),
    .out(O[4]), .sel(Shift));
  Multiplexer #(.select(3), .enable("false")) multiplexer_2 (
    .in0(A[3]), .in1(A[2]), .in2(A[1]), .in3(A[0]), .in4(1'b0), .in5(1'b0), .in6(1'b0), .in7(1'b0),
    .out(O[3]), .sel(Shift));
  Multiplexer #(.select(3), .enable("false")) multiplexer_3 (
    .in0(A[2]), .in1(A[1]), .in2(A[0]), .in3(1'b0), .in4(1'b0), .in5(1'b0), .in6(1'b0), .in7(1'b0),
    .out(O[2]), .sel(Shift));
  Multiplexer #(.select(3), .enable("false")) multiplexer_4 (
    .in0(A[1]), .in1(A[0]), .in2(1'b0), .in3(1'b0), .in4(1'b0), .in5(1'b0), .in6(1'b0), .in7(1'b0),
    .out(O[1]), .sel(Shift));
  Multiplexer #(.select(3), .enable("false")) multiplexer_5 (
    .in0(A[0]), .in1(1'b0), .in2(1'b0), .in3(1'b0), .in4(1'b0), .in5(1'b0), .in6(1'b0), .in7(1'b0),
    .out(O[0]), .sel(Shift));

  // Notes on the sheet:
  //   5-bit Left Shift
endmodule
