// Logisim project 5-bit 4 to 1 MUX.circ as structural Verilog: 1 circuit, main circuit main
module main (
  input  [4:0] A,
  input  [4:0] B,
  input  [4:0] C,
  input  [4:0] D,
  output [4:0] O
);

  Multiplexer #(.select(2), .width(4), .enable("false")) multiplexer_1 ();  // open: in0, in1, in2, in3, out, sel
endmodule
